# Fritzing sketch Fritzing_basic (saved by Fritzing 0.9.3b)

parts:
  M1 = DC Motor
  Raspberry_Pi_1 = Raspberry Pi 3 [part_number=RPI-3-V1.2]
  M2 = DC Motor
  U1 = L298 [package=multiwatt15]
  PWM1 = PCA9685 16x12-bit PWM Breakout
  J1 = Basic Servo
  J2 = Basic Servo
  J3 = Basic Servo
  J4 = Basic Servo
  J5 = Basic Servo
  BAT1 = BC9VPC [package=bc9vpc]
  IC1 = L293D [package=THT]
  J6 = Infrared Proximity Sensor  # not connected
  U3 = LIPO-2000mAh [package=lipo-2000]
  J7 = Basic Servo
  U4 = SWITCH-SPST-2 [package=switch-spst-vertical]
  hc-sr1 = hc-sr04
  hc-sr2 = hc-sr04
  Pololu_A1 = Pololu A4988 [package=SO16]
  VCC1 = 4 x AAA Battery Mount  # not connected
  VCC2 = Battery block 9V
  M3 = Stepper Motor - Bipolar

nets:
  N1: M1.pin_1, U1.OUT3
  N2: M1.pin_2, U1.OUT4
  N3: Raspberry_Pi_1.GPIO2, PWM1.no_name_yet#504
  N4: Raspberry_Pi_1.GPIO3, PWM1.no_name_yet#503
  GND: Raspberry_Pi_1.GND, U1.GND, BAT1.V-, IC1.0V
  N5: Raspberry_Pi_1.GIPO9, Pololu_A1.STEP
  N6: Raspberry_Pi_1.GIPO11, Pololu_A1.DIR
  N7: Raspberry_Pi_1.GIPO19, U1.ENA
  N8: Raspberry_Pi_1.GIPO26, U1.ENB
  N9: Raspberry_Pi_1.GIPO21, U1.IN1
  N10: Raspberry_Pi_1.GIPO20, U1.IN2
  N11: Raspberry_Pi_1.GIPO16, U1.IN3
  N12: Raspberry_Pi_1.GIPO12, U1.IN4
  N13: Raspberry_Pi_1.5V, IC1.+Vmotor
  N14: M2.pin_1, U1.OUT1
  N15: M2.pin_2, U1.OUT2
  N16: PWM1.no_name_yet#0, J1.pulse
  N17: PWM1.no_name_yet#1, J5.pulse
  N18: PWM1.no_name_yet#2, J3.pulse
  N19: PWM1.no_name_yet#3, J4.pulse
  N20: PWM1.no_name_yet#4, J2.pulse
  N21: PWM1.no_name_yet#7, J7.pulse
  N22: PWM1.no_name_yet#8, hc-sr1.Trig
  N23: PWM1.no_name_yet#11, hc-sr2.Trig
  VCC: PWM1.no_name_yet#100, PWM1.no_name_yet#101, PWM1.no_name_yet#102, PWM1.no_name_yet#103, PWM1.no_name_yet#104, PWM1.no_name_yet#107, PWM1.no_name_yet#108, PWM1.no_name_yet#111, hc-sr1.VCC, hc-sr2.VCC
  GND_2: PWM1.no_name_yet#501, PWM1.no_name_yet#1000, PWM1.no_name_yet#1001, PWM1.no_name_yet#1002, PWM1.no_name_yet#1003, PWM1.no_name_yet#1004, PWM1.no_name_yet#1007, PWM1.no_name_yet#1008, PWM1.no_name_yet#1011, U3.-, hc-sr1.GND, hc-sr2.GND
  N24: PWM1.no_name_yet#505, U3.+
  N25: BAT1.V+, U4.P
  N26: IC1.+V, U4.O
  N27: Pololu_A1.RESET, Pololu_A1.SLEEP
  N28: Pololu_A1.1B, M3.D
  N29: Pololu_A1.1A, M3.B
  N30: Pololu_A1.2A, M3.C
  N31: Pololu_A1.2B, M3.A
  N32: Pololu_A1.GND, VCC2.-
  N33: Pololu_A1.VMOT, VCC2.+
